// Logisim project 1906137_CS4401_Assignment-1.circ as structural Verilog: 10 circuits, main circuit Main
module L_1_Bit_Full_Adder_1807bcc1 (
  input  Cin,
  input  A,
  input  B,
  output S,
  output Cout
);

  wire and_1_out, and_2_out, xor_1_out;

  xor xor_1 (xor_1_out, A, B);
  and and_1 (and_1_out, B, A);
  xor xor_2 (S, xor_1_out, Cin);
  and and_2 (and_2_out, xor_1_out, Cin);
  or or_1 (Cout, and_2_out, and_1_out);
endmodule

module L_32_Bit_Adder_9e9753e4 (
  input  [31:0] B,
  input  [31:0] A,
  input  Sub,
  output OF,
  output Cout,
  output [31:0] S
);

  wire l_1_bit_full_adder_1807bcc1_1_cout, l_1_bit_full_adder_1807bcc1_2_cout,
       l_1_bit_full_adder_1807bcc1_3_cout, l_1_bit_full_adder_1807bcc1_4_cout,
       l_1_bit_full_adder_1807bcc1_5_cout, l_1_bit_full_adder_1807bcc1_6_cout,
       l_1_bit_full_adder_1807bcc1_7_cout, l_1_bit_full_adder_1807bcc1_8_cout,
       l_1_bit_full_adder_1807bcc1_9_cout, l_1_bit_full_adder_1807bcc1_10_cout,
       l_1_bit_full_adder_1807bcc1_11_cout, l_1_bit_full_adder_1807bcc1_12_cout,
       l_1_bit_full_adder_1807bcc1_13_cout, l_1_bit_full_adder_1807bcc1_14_cout,
       l_1_bit_full_adder_1807bcc1_15_cout, l_1_bit_full_adder_1807bcc1_16_cout,
       l_1_bit_full_adder_1807bcc1_17_cout, l_1_bit_full_adder_1807bcc1_18_cout,
       l_1_bit_full_adder_1807bcc1_19_cout, l_1_bit_full_adder_1807bcc1_20_cout,
       l_1_bit_full_adder_1807bcc1_21_cout, l_1_bit_full_adder_1807bcc1_22_cout,
       l_1_bit_full_adder_1807bcc1_23_cout, l_1_bit_full_adder_1807bcc1_24_cout,
       l_1_bit_full_adder_1807bcc1_25_cout, l_1_bit_full_adder_1807bcc1_26_cout,
       l_1_bit_full_adder_1807bcc1_27_cout, l_1_bit_full_adder_1807bcc1_28_cout,
       l_1_bit_full_adder_1807bcc1_29_cout, l_1_bit_full_adder_1807bcc1_30_cout,
       l_1_bit_full_adder_1807bcc1_31_cout, l_1_bit_full_adder_1807bcc1_32_cout, xor_3_out, xor_4_out,
       xor_5_out, xor_6_out, xor_7_out, xor_8_out, xor_9_out, xor_10_out, xor_11_out, xor_12_out, xor_13_out,
       xor_14_out, xor_15_out, xor_16_out, xor_17_out, xor_18_out, xor_19_out, xor_20_out, xor_21_out,
       xor_22_out, xor_23_out, xor_24_out, xor_25_out, xor_26_out, xor_27_out, xor_28_out, xor_29_out,
       xor_30_out, xor_31_out, xor_32_out, xor_33_out, xor_34_out, xor_35_out;

  xor xor_1 (Cout, Sub, l_1_bit_full_adder_1807bcc1_1_cout);
  xor xor_2 (OF, l_1_bit_full_adder_1807bcc1_2_cout, l_1_bit_full_adder_1807bcc1_1_cout);
  xor xor_3 (xor_3_out, B[31], Sub);
  L_1_Bit_Full_Adder_1807bcc1 l_1_bit_full_adder_1807bcc1_1 (
    .A(xor_3_out), .B(A[31]), .S(S[31]), .Cout(l_1_bit_full_adder_1807bcc1_1_cout),
    .Cin(l_1_bit_full_adder_1807bcc1_2_cout));
  xor xor_4 (xor_4_out, B[30], Sub);
  L_1_Bit_Full_Adder_1807bcc1 l_1_bit_full_adder_1807bcc1_2 (
    .A(xor_4_out), .B(A[30]), .S(S[30]), .Cout(l_1_bit_full_adder_1807bcc1_2_cout),
    .Cin(l_1_bit_full_adder_1807bcc1_3_cout));
  xor xor_5 (xor_5_out, B[29], Sub);
  L_1_Bit_Full_Adder_1807bcc1 l_1_bit_full_adder_1807bcc1_3 (
    .A(xor_5_out), .B(A[29]), .S(S[29]), .Cout(l_1_bit_full_adder_1807bcc1_3_cout),
    .Cin(l_1_bit_full_adder_1807bcc1_4_cout));
  xor xor_6 (xor_6_out, B[28], Sub);
  L_1_Bit_Full_Adder_1807bcc1 l_1_bit_full_adder_1807bcc1_4 (
    .A(xor_6_out), .B(A[28]), .S(S[28]), .Cout(l_1_bit_full_adder_1807bcc1_4_cout),
    .Cin(l_1_bit_full_adder_1807bcc1_5_cout));
  xor xor_7 (xor_7_out, B[27], Sub);
  L_1_Bit_Full_Adder_1807bcc1 l_1_bit_full_adder_1807bcc1_5 (
    .A(xor_7_out), .B(A[27]), .S(S[27]), .Cout(l_1_bit_full_adder_1807bcc1_5_cout),
    .Cin(l_1_bit_full_adder_1807bcc1_6_cout));
  xor xor_8 (xor_8_out, B[26], Sub);
  L_1_Bit_Full_Adder_1807bcc1 l_1_bit_full_adder_1807bcc1_6 (
    .A(xor_8_out), .B(A[26]), .S(S[26]), .Cout(l_1_bit_full_adder_1807bcc1_6_cout),
    .Cin(l_1_bit_full_adder_1807bcc1_7_cout));
  xor xor_9 (xor_9_out, B[25], Sub);
  L_1_Bit_Full_Adder_1807bcc1 l_1_bit_full_adder_1807bcc1_7 (
    .A(xor_9_out), .B(A[25]), .S(S[25]), .Cout(l_1_bit_full_adder_1807bcc1_7_cout),
    .Cin(l_1_bit_full_adder_1807bcc1_8_cout));
  xor xor_10 (xor_10_out, B[24], Sub);
  L_1_Bit_Full_Adder_1807bcc1 l_1_bit_full_adder_1807bcc1_8 (
    .A(xor_10_out), .B(A[24]), .S(S[24]), .Cout(l_1_bit_full_adder_1807bcc1_8_cout),
    .Cin(l_1_bit_full_adder_1807bcc1_9_cout));
  xor xor_11 (xor_11_out, B[23], Sub);
  L_1_Bit_Full_Adder_1807bcc1 l_1_bit_full_adder_1807bcc1_9 (
    .A(xor_11_out), .B(A[23]), .S(S[23]), .Cout(l_1_bit_full_adder_1807bcc1_9_cout),
    .Cin(l_1_bit_full_adder_1807bcc1_10_cout));
  xor xor_12 (xor_12_out, B[22], Sub);
  L_1_Bit_Full_Adder_1807bcc1 l_1_bit_full_adder_1807bcc1_10 (
    .A(xor_12_out), .B(A[22]), .S(S[22]), .Cout(l_1_bit_full_adder_1807bcc1_10_cout),
    .Cin(l_1_bit_full_adder_1807bcc1_11_cout));
  xor xor_13 (xor_13_out, B[21], Sub);
  L_1_Bit_Full_Adder_1807bcc1 l_1_bit_full_adder_1807bcc1_11 (
    .A(xor_13_out), .B(A[21]), .S(S[21]), .Cout(l_1_bit_full_adder_1807bcc1_11_cout),
    .Cin(l_1_bit_full_adder_1807bcc1_12_cout));
  xor xor_14 (xor_14_out, B[20], Sub);
  L_1_Bit_Full_Adder_1807bcc1 l_1_bit_full_adder_1807bcc1_12 (
    .A(xor_14_out), .B(A[20]), .S(S[20]), .Cout(l_1_bit_full_adder_1807bcc1_12_cout),
    .Cin(l_1_bit_full_adder_1807bcc1_13_cout));
  xor xor_15 (xor_15_out, B[19], Sub);
  L_1_Bit_Full_Adder_1807bcc1 l_1_bit_full_adder_1807bcc1_13 (
    .A(xor_15_out), .B(A[19]), .S(S[19]), .Cout(l_1_bit_full_adder_1807bcc1_13_cout),
    .Cin(l_1_bit_full_adder_1807bcc1_14_cout));
  xor xor_16 (xor_16_out, B[18], Sub);
  L_1_Bit_Full_Adder_1807bcc1 l_1_bit_full_adder_1807bcc1_14 (
    .A(xor_16_out), .B(A[18]), .S(S[18]), .Cout(l_1_bit_full_adder_1807bcc1_14_cout),
    .Cin(l_1_bit_full_adder_1807bcc1_15_cout));
  xor xor_17 (xor_17_out, B[17], Sub);
  L_1_Bit_Full_Adder_1807bcc1 l_1_bit_full_adder_1807bcc1_15 (
    .A(xor_17_out), .B(A[17]), .S(S[17]), .Cout(l_1_bit_full_adder_1807bcc1_15_cout),
    .Cin(l_1_bit_full_adder_1807bcc1_16_cout));
  xor xor_18 (xor_18_out, B[16], Sub);
  L_1_Bit_Full_Adder_1807bcc1 l_1_bit_full_adder_1807bcc1_16 (
    .A(xor_18_out), .B(A[16]), .S(S[16]), .Cout(l_1_bit_full_adder_1807bcc1_16_cout),
    .Cin(l_1_bit_full_adder_1807bcc1_17_cout));
  xor xor_19 (xor_19_out, B[15], Sub);
  L_1_Bit_Full_Adder_1807bcc1 l_1_bit_full_adder_1807bcc1_17 (
    .A(xor_19_out), .B(A[15]), .S(S[15]), .Cout(l_1_bit_full_adder_1807bcc1_17_cout),
    .Cin(l_1_bit_full_adder_1807bcc1_18_cout));
  xor xor_20 (xor_20_out, B[14], Sub);
  L_1_Bit_Full_Adder_1807bcc1 l_1_bit_full_adder_1807bcc1_18 (
    .A(xor_20_out), .B(A[14]), .S(S[14]), .Cout(l_1_bit_full_adder_1807bcc1_18_cout),
    .Cin(l_1_bit_full_adder_1807bcc1_19_cout));
  xor xor_21 (xor_21_out, B[13], Sub);
  L_1_Bit_Full_Adder_1807bcc1 l_1_bit_full_adder_1807bcc1_19 (
    .A(xor_21_out), .B(A[13]), .S(S[13]), .Cout(l_1_bit_full_adder_1807bcc1_19_cout),
    .Cin(l_1_bit_full_adder_1807bcc1_20_cout));
  xor xor_22 (xor_22_out, B[12], Sub);
  L_1_Bit_Full_Adder_1807bcc1 l_1_bit_full_adder_1807bcc1_20 (
    .A(xor_22_out), .B(A[12]), .S(S[12]), .Cout(l_1_bit_full_adder_1807bcc1_20_cout),
    .Cin(l_1_bit_full_adder_1807bcc1_21_cout));
  xor xor_23 (xor_23_out, B[11], Sub);
  L_1_Bit_Full_Adder_1807bcc1 l_1_bit_full_adder_1807bcc1_21 (
    .A(xor_23_out), .B(A[11]), .S(S[11]), .Cout(l_1_bit_full_adder_1807bcc1_21_cout),
    .Cin(l_1_bit_full_adder_1807bcc1_22_cout));
  xor xor_24 (xor_24_out, B[10], Sub);
  L_1_Bit_Full_Adder_1807bcc1 l_1_bit_full_adder_1807bcc1_22 (
    .A(xor_24_out), .B(A[10]), .S(S[10]), .Cout(l_1_bit_full_adder_1807bcc1_22_cout),
    .Cin(l_1_bit_full_adder_1807bcc1_23_cout));
  xor xor_25 (xor_25_out, B[9], Sub);
  L_1_Bit_Full_Adder_1807bcc1 l_1_bit_full_adder_1807bcc1_23 (
    .A(xor_25_out), .B(A[9]), .S(S[9]), .Cout(l_1_bit_full_adder_1807bcc1_23_cout),
    .Cin(l_1_bit_full_adder_1807bcc1_24_cout));
  xor xor_26 (xor_26_out, B[8], Sub);
  L_1_Bit_Full_Adder_1807bcc1 l_1_bit_full_adder_1807bcc1_24 (
    .A(xor_26_out), .B(A[8]), .S(S[8]), .Cout(l_1_bit_full_adder_1807bcc1_24_cout),
    .Cin(l_1_bit_full_adder_1807bcc1_25_cout));
  xor xor_27 (xor_27_out, B[7], Sub);
  L_1_Bit_Full_Adder_1807bcc1 l_1_bit_full_adder_1807bcc1_25 (
    .A(xor_27_out), .B(A[7]), .S(S[7]), .Cout(l_1_bit_full_adder_1807bcc1_25_cout),
    .Cin(l_1_bit_full_adder_1807bcc1_26_cout));
  xor xor_28 (xor_28_out, B[6], Sub);
  L_1_Bit_Full_Adder_1807bcc1 l_1_bit_full_adder_1807bcc1_26 (
    .A(xor_28_out), .B(A[6]), .S(S[6]), .Cout(l_1_bit_full_adder_1807bcc1_26_cout),
    .Cin(l_1_bit_full_adder_1807bcc1_27_cout));
  xor xor_29 (xor_29_out, B[5], Sub);
  L_1_Bit_Full_Adder_1807bcc1 l_1_bit_full_adder_1807bcc1_27 (
    .A(xor_29_out), .B(A[5]), .S(S[5]), .Cout(l_1_bit_full_adder_1807bcc1_27_cout),
    .Cin(l_1_bit_full_adder_1807bcc1_28_cout));
  xor xor_30 (xor_30_out, B[4], Sub);
  L_1_Bit_Full_Adder_1807bcc1 l_1_bit_full_adder_1807bcc1_28 (
    .A(xor_30_out), .B(A[4]), .S(S[4]), .Cout(l_1_bit_full_adder_1807bcc1_28_cout),
    .Cin(l_1_bit_full_adder_1807bcc1_29_cout));
  xor xor_31 (xor_31_out, B[3], Sub);
  L_1_Bit_Full_Adder_1807bcc1 l_1_bit_full_adder_1807bcc1_29 (
    .A(xor_31_out), .B(A[3]), .S(S[3]), .Cout(l_1_bit_full_adder_1807bcc1_29_cout),
    .Cin(l_1_bit_full_adder_1807bcc1_30_cout));
  xor xor_32 (xor_32_out, B[2], Sub);
  L_1_Bit_Full_Adder_1807bcc1 l_1_bit_full_adder_1807bcc1_30 (
    .A(xor_32_out), .B(A[2]), .S(S[2]), .Cout(l_1_bit_full_adder_1807bcc1_30_cout),
    .Cin(l_1_bit_full_adder_1807bcc1_31_cout));
  xor xor_33 (xor_33_out, B[1], Sub);
  L_1_Bit_Full_Adder_1807bcc1 l_1_bit_full_adder_1807bcc1_31 (
    .A(xor_33_out), .B(A[1]), .S(S[1]), .Cout(l_1_bit_full_adder_1807bcc1_31_cout),
    .Cin(l_1_bit_full_adder_1807bcc1_32_cout));
  xor xor_34 (xor_34_out, B[0], Sub);
  L_1_Bit_Full_Adder_1807bcc1 l_1_bit_full_adder_1807bcc1_32 (
    .A(xor_34_out), .B(A[0]), .S(S[0]), .Cout(l_1_bit_full_adder_1807bcc1_32_cout), .Cin(xor_35_out));
  xor xor_35 (xor_35_out, 1'b0, Sub);
endmodule

module L_32_Bit_OR_45ca753a (
  input  [31:0] in_1,
  input  [31:0] in_2,
  output [31:0] out_3
);

  or or_1 (out_3[0], in_1[0], in_2[0]);
  or or_2 (out_3[1], in_1[1], in_2[1]);
  or or_3 (out_3[2], in_1[2], in_2[2]);
  or or_4 (out_3[3], in_1[3], in_2[3]);
  or or_5 (out_3[4], in_1[4], in_2[4]);
  or or_6 (out_3[5], in_1[5], in_2[5]);
  or or_7 (out_3[6], in_1[6], in_2[6]);
  or or_8 (out_3[7], in_1[7], in_2[7]);
  or or_9 (out_3[8], in_1[8], in_2[8]);
  or or_10 (out_3[9], in_1[9], in_2[9]);
  or or_11 (out_3[10], in_1[10], in_2[10]);
  or or_12 (out_3[11], in_1[11], in_2[11]);
  or or_13 (out_3[12], in_1[12], in_2[12]);
  or or_14 (out_3[13], in_1[13], in_2[13]);
  or or_15 (out_3[14], in_1[14], in_2[14]);
  or or_16 (out_3[15], in_1[15], in_2[15]);
  or or_17 (out_3[16], in_1[16], in_2[16]);
  or or_18 (out_3[17], in_1[17], in_2[17]);
  or or_19 (out_3[18], in_1[18], in_2[18]);
  or or_20 (out_3[19], in_1[19], in_2[19]);
  or or_21 (out_3[20], in_1[20], in_2[20]);
  or or_22 (out_3[21], in_1[21], in_2[21]);
  or or_23 (out_3[22], in_1[22], in_2[22]);
  or or_24 (out_3[23], in_1[23], in_2[23]);
  or or_25 (out_3[24], in_1[24], in_2[24]);
  or or_26 (out_3[25], in_1[25], in_2[25]);
  or or_27 (out_3[26], in_1[26], in_2[26]);
  or or_28 (out_3[27], in_1[27], in_2[27]);
  or or_29 (out_3[28], in_1[28], in_2[28]);
  or or_30 (out_3[29], in_1[29], in_2[29]);
  or or_31 (out_3[30], in_1[30], in_2[30]);
  or or_32 (out_3[31], in_1[31], in_2[31]);
endmodule

module L_32_Bit_AND_ab209484 (
  input  [31:0] in_1,
  input  [31:0] in_2,
  output [31:0] out_3
);

  and and_1 (out_3[0], in_1[0], in_2[0]);
  and and_2 (out_3[1], in_1[1], in_2[1]);
  and and_3 (out_3[2], in_1[2], in_2[2]);
  and and_4 (out_3[3], in_1[3], in_2[3]);
  and and_5 (out_3[4], in_1[4], in_2[4]);
  and and_6 (out_3[5], in_1[5], in_2[5]);
  and and_7 (out_3[6], in_1[6], in_2[6]);
  and and_8 (out_3[7], in_1[7], in_2[7]);
  and and_9 (out_3[8], in_1[8], in_2[8]);
  and and_10 (out_3[9], in_1[9], in_2[9]);
  and and_11 (out_3[10], in_1[10], in_2[10]);
  and and_12 (out_3[11], in_1[11], in_2[11]);
  and and_13 (out_3[12], in_1[12], in_2[12]);
  and and_14 (out_3[13], in_1[13], in_2[13]);
  and and_15 (out_3[14], in_1[14], in_2[14]);
  and and_16 (out_3[15], in_1[15], in_2[15]);
  and and_17 (out_3[16], in_1[16], in_2[16]);
  and and_18 (out_3[17], in_1[17], in_2[17]);
  and and_19 (out_3[18], in_1[18], in_2[18]);
  and and_20 (out_3[19], in_1[19], in_2[19]);
  and and_21 (out_3[20], in_1[20], in_2[20]);
  and and_22 (out_3[21], in_1[21], in_2[21]);
  and and_23 (out_3[22], in_1[22], in_2[22]);
  and and_24 (out_3[23], in_1[23], in_2[23]);
  and and_25 (out_3[24], in_1[24], in_2[24]);
  and and_26 (out_3[25], in_1[25], in_2[25]);
  and and_27 (out_3[26], in_1[26], in_2[26]);
  and and_28 (out_3[27], in_1[27], in_2[27]);
  and and_29 (out_3[28], in_1[28], in_2[28]);
  and and_30 (out_3[29], in_1[29], in_2[29]);
  and and_31 (out_3[30], in_1[30], in_2[30]);
  and and_32 (out_3[31], in_1[31], in_2[31]);
endmodule

module L_32_Bit_NOT_b85b74d2 (
  input  [31:0] in_1,
  output [31:0] out_2
);

  not not_1 (out_2[0], in_1[0]);
  not not_2 (out_2[1], in_1[1]);
  not not_3 (out_2[2], in_1[2]);
  not not_4 (out_2[3], in_1[3]);
  not not_5 (out_2[4], in_1[4]);
  not not_6 (out_2[5], in_1[5]);
  not not_7 (out_2[6], in_1[6]);
  not not_8 (out_2[7], in_1[7]);
  not not_9 (out_2[8], in_1[8]);
  not not_10 (out_2[9], in_1[9]);
  not not_11 (out_2[10], in_1[10]);
  not not_12 (out_2[11], in_1[11]);
  not not_13 (out_2[12], in_1[12]);
  not not_14 (out_2[13], in_1[13]);
  not not_15 (out_2[14], in_1[14]);
  not not_16 (out_2[15], in_1[15]);
  not not_17 (out_2[16], in_1[16]);
  not not_18 (out_2[17], in_1[17]);
  not not_19 (out_2[18], in_1[18]);
  not not_20 (out_2[19], in_1[19]);
  not not_21 (out_2[20], in_1[20]);
  not not_22 (out_2[21], in_1[21]);
  not not_23 (out_2[22], in_1[22]);
  not not_24 (out_2[23], in_1[23]);
  not not_25 (out_2[24], in_1[24]);
  not not_26 (out_2[25], in_1[25]);
  not not_27 (out_2[26], in_1[26]);
  not not_28 (out_2[27], in_1[27]);
  not not_29 (out_2[28], in_1[28]);
  not not_30 (out_2[29], in_1[29]);
  not not_31 (out_2[30], in_1[30]);
  not not_32 (out_2[31], in_1[31]);
endmodule

module L_32_Bit_Negator_d65d074c (
  input  [31:0] in_1,
  output [31:0] out_2
);

  wire [31:0] l_32_bit_not_b85b74d2_1_out_2;

  L_32_Bit_NOT_b85b74d2 l_32_bit_not_b85b74d2_1 (.in_1(in_1), .out_2(l_32_bit_not_b85b74d2_1_out_2));
  L_32_Bit_Adder_9e9753e4 l_32_bit_adder_9e9753e4_1 (
    .A(l_32_bit_not_b85b74d2_1_out_2), .S(out_2), .Sub(1'b0), .B(32'h1));  // open: OF, Cout
endmodule

module L_4_Bit_Manual_Multiplier_8a8d0933 (
  input  [3:0] M,
  input  [3:0] Q,
  input  Init,
  input  Shift,
  input  Load
);

  wire clock_1_out, shift_register_2_p1, shift_register_3_p2, shift_register_3_p3, shift_register_3_p7;
  wire [2:0] comparator_1_gt;
  wire [3:0] adder_1_out, multiplexer_1_out, subtractor_1_out, undriven;

  Multiplexer #(.select(3), .width(4)) multiplexer_1 (
    .in1(subtractor_1_out), .in2(undriven), .in4(adder_1_out), .out(multiplexer_1_out), .sel(comparator_1_gt));  // open: in0, in3, in5, in6, in7, en
  Clock clock_1 (.out(clock_1_out));
  // Shift_Register #(.length(4)) shift_register_1: pin names not known; wires that end beside it: Shift, undriven[3], clock_1_out, Load, multiplexer_1_out[3], multiplexer_1_out[2], multiplexer_1_out[1], multiplexer_1_out[0]
  Subtractor #(.width(4)) subtractor_1 (.a(undriven), .b(M), .out(subtractor_1_out), .bin(1'b0));  // open: bout
  Adder #(.width(4)) adder_1 (.a(undriven), .b(M), .out(adder_1_out), .cin(1'b0));  // open: cout
  // Shift_Register #(.length(4)) shift_register_2: pin names not known; wires that end beside it: shift_register_2_p1, Shift, shift_register_2_p1, clock_1_out, Init, Q[3], Q[2], Q[1]
  // Shift_Register #(.length(1)) shift_register_3: pin names not known; wires that end beside it: Q[0], shift_register_3_p2, shift_register_3_p3, Shift, shift_register_3_p3, clock_1_out, shift_register_3_p7
  Comparator #(.width(1)) comparator_1 (
    .a(shift_register_3_p7), .b(shift_register_3_p2), .gt(comparator_1_gt[0]), .eq(comparator_1_gt[1]),
    .lt(comparator_1_gt[2]));
  Multiplier multiplier_1 ();  // open: a, b, out, cin, cout
endmodule

module L_32_Bit_Manual_Multiplier_9beca478 (
  input  [31:0] M,
  input  [31:0] Q,
  input  Init,
  output [31:0] MSB,
  output [31:0] LSB
);

  wire and_1_out, and_2_out, Clk_out, counter_1_carry, not_1_out, not_2_out, not_3_out, shift_register_2_p16,
       shift_register_3_p17, shift_register_3_p21, xnor_1_out;
  wire [31:0] l_32_bit_adder_9e9753e4_1_s, shift_register_2_p15, undriven, undriven_2;

  Clock Clk (.out(Clk_out));
  not not_1 (not_1_out, counter_1_carry);
  and and_1 (and_1_out, Clk_out, not_1_out);
  not not_2 (not_2_out, and_1_out);
  Counter #(.width(6), .max('h3f), .ongoal("stay")) counter_1 (
    .carry(counter_1_carry), .clk(and_1_out));  // open: load, D, count, Q, clr
  // Shift_Register #(.length(32)) shift_register_1: pin names not known; wires that end beside it: not_2_out, undriven[31], and_1_out, and_1_out, shift_register_2_p15[31], shift_register_2_p15[30], shift_register_2_p15[29], shift_register_2_p15[28], shift_register_2_p15[27], shift_register_2_p15[26], shift_register_2_p15[25], shift_register_2_p15[24], shift_register_2_p15[23], shift_register_2_p15[22], shift_register_2_p15[21], shift_register_2_p15[20], shift_register_2_p15[19], shift_register_2_p15[18], shift_register_2_p15[17], shift_register_2_p15[16], shift_register_2_p15[15]
  Multiplexer #(.width(32)) multiplexer_1 (
    .in0({32{1'b0}}), .in1(undriven), .out(MSB), .sel(counter_1_carry));  // open: en
  Multiplexer #(.width(32)) multiplexer_2 (
    .in0({32{1'b0}}), .in1(undriven_2), .out(LSB), .sel(counter_1_carry));  // open: en
  // Shift_Register #(.length(32)) shift_register_2: pin names not known; wires that end beside it: shift_register_2_p15[14], shift_register_2_p15[13], shift_register_2_p15[12], shift_register_2_p15[11], shift_register_2_p15[10], shift_register_2_p15[9], shift_register_2_p15[8], shift_register_2_p15[7], shift_register_2_p15[6], shift_register_2_p15[5], shift_register_2_p15[4], shift_register_2_p15[3], shift_register_2_p15[2], shift_register_2_p15[1], shift_register_2_p15[0], shift_register_2_p16, not_2_out, shift_register_2_p16, and_1_out, Init, Q[31], Q[30], Q[29], Q[28], Q[27], Q[26], Q[25], Q[24], Q[23], Q[22], Q[21], Q[20], Q[19], Q[18], Q[17], Q[16]
  Multiplexer #(.width(32)) multiplexer_3 (
    .in0(l_32_bit_adder_9e9753e4_1_s), .in1(undriven), .out(shift_register_2_p15), .sel(xnor_1_out));  // open: en
  L_32_Bit_Adder_9e9753e4 l_32_bit_adder_9e9753e4_1 (
    .A(undriven), .S(l_32_bit_adder_9e9753e4_1_s), .Sub(and_2_out), .B(M));  // open: OF, Cout
  xnor xnor_1 (xnor_1_out, undriven_2[0], shift_register_3_p21);
  and and_2 (and_2_out, undriven_2[0], not_3_out);
  not not_3 (not_3_out, shift_register_3_p21);
  // Shift_Register #(.length(1)) shift_register_3: pin names not known; wires that end beside it: Q[15], Q[14], Q[13], Q[12], Q[11], Q[10], Q[9], Q[8], Q[7], Q[6], Q[5], Q[4], Q[3], Q[2], Q[1], Q[0], shift_register_3_p17, not_2_out, shift_register_3_p17, and_1_out, shift_register_3_p21
endmodule

module Main (
  input  [31:0] a,
  input  [31:0] b,
  input  [2:0] counter,
  output [31:0] \output 
);

  wire [31:0] divider_1_out, l_32_bit_adder_9e9753e4_1_s, l_32_bit_adder_9e9753e4_2_s,
       l_32_bit_and_ab209484_1_out_3, l_32_bit_negator_d65d074c_1_out_2, l_32_bit_not_b85b74d2_1_out_2,
       l_32_bit_or_45ca753a_1_out_3, multiplier_1_out;

  L_32_Bit_NOT_b85b74d2 l_32_bit_not_b85b74d2_1 (.in_1(a), .out_2(l_32_bit_not_b85b74d2_1_out_2));
  L_32_Bit_Negator_d65d074c l_32_bit_negator_d65d074c_1 (.in_1(a), .out_2(l_32_bit_negator_d65d074c_1_out_2));
  L_32_Bit_AND_ab209484 l_32_bit_and_ab209484_1 (.in_2(b), .in_1(a), .out_3(l_32_bit_and_ab209484_1_out_3));
  L_32_Bit_OR_45ca753a l_32_bit_or_45ca753a_1 (.in_2(b), .in_1(a), .out_3(l_32_bit_or_45ca753a_1_out_3));
  L_32_Bit_Adder_9e9753e4 l_32_bit_adder_9e9753e4_1 (
    .A(a), .S(l_32_bit_adder_9e9753e4_1_s), .Sub(1'b1), .B(b));  // open: OF, Cout
  L_32_Bit_Adder_9e9753e4 l_32_bit_adder_9e9753e4_2 (
    .A(a), .S(l_32_bit_adder_9e9753e4_2_s), .Sub(1'b0), .B(b));  // open: OF, Cout
  Multiplier #(.width(32)) multiplier_1 (.a(a), .b(b), .out(multiplier_1_out));  // open: cin, cout
  Divider #(.width(32)) divider_1 (.a(a), .b(b), .out(divider_1_out));  // open: upper, rem
  Multiplexer #(.select(3), .width(32)) multiplexer_1 (
    .in0(l_32_bit_not_b85b74d2_1_out_2), .in1(l_32_bit_negator_d65d074c_1_out_2),
    .in2(l_32_bit_and_ab209484_1_out_3), .in3(l_32_bit_or_45ca753a_1_out_3),
    .in4(l_32_bit_adder_9e9753e4_1_s), .in5(l_32_bit_adder_9e9753e4_2_s), .in6(multiplier_1_out),
    .in7(divider_1_out), .out(\output ), .sel(counter));  // open: en

  // Notes on the sheet:
  //   BATCH : CSE 2
  //   ASSIGNMENT - 1
  //   NOT
  //   NEGATION
  //   AND
  //   OR
  //   NAME : ABHIRAJ YOGESH SRIVASTAVA
  //   ROLL NO. ; 1906137
  //   COURSE CODE : CS4401
  //   SUBTRACTOR
  //   ADDER
  //   MULTIPLIER
  //   DIVIDER
  //   000 - NOT
  //   010 - AND
  //   011 - OR
  //   001 - NEGATION
  //   100 - SUBTRACTOR
  //   101 - ADDER
  //   110 - MULTIPLIER
  //   111 - DIVIDER
  //   COUNTER CODES AND THEIR RESPECTIVE FUNCTIONS
endmodule

module L_32_Bit_Subtractor_4e06e2f8 (
  input  [31:0] B,
  input  [31:0] A,
  input  Sub,
  output OF,
  output Cout,
  output [31:0] S
);

  wire l_1_bit_full_adder_1807bcc1_1_cout, l_1_bit_full_adder_1807bcc1_2_cout,
       l_1_bit_full_adder_1807bcc1_3_cout, l_1_bit_full_adder_1807bcc1_4_cout,
       l_1_bit_full_adder_1807bcc1_5_cout, l_1_bit_full_adder_1807bcc1_6_cout,
       l_1_bit_full_adder_1807bcc1_7_cout, l_1_bit_full_adder_1807bcc1_8_cout,
       l_1_bit_full_adder_1807bcc1_9_cout, l_1_bit_full_adder_1807bcc1_10_cout,
       l_1_bit_full_adder_1807bcc1_11_cout, l_1_bit_full_adder_1807bcc1_12_cout,
       l_1_bit_full_adder_1807bcc1_13_cout, l_1_bit_full_adder_1807bcc1_14_cout,
       l_1_bit_full_adder_1807bcc1_15_cout, l_1_bit_full_adder_1807bcc1_16_cout,
       l_1_bit_full_adder_1807bcc1_17_cout, l_1_bit_full_adder_1807bcc1_18_cout,
       l_1_bit_full_adder_1807bcc1_19_cout, l_1_bit_full_adder_1807bcc1_20_cout,
       l_1_bit_full_adder_1807bcc1_21_cout, l_1_bit_full_adder_1807bcc1_22_cout,
       l_1_bit_full_adder_1807bcc1_23_cout, l_1_bit_full_adder_1807bcc1_24_cout,
       l_1_bit_full_adder_1807bcc1_25_cout, l_1_bit_full_adder_1807bcc1_26_cout,
       l_1_bit_full_adder_1807bcc1_27_cout, l_1_bit_full_adder_1807bcc1_28_cout,
       l_1_bit_full_adder_1807bcc1_29_cout, l_1_bit_full_adder_1807bcc1_30_cout,
       l_1_bit_full_adder_1807bcc1_31_cout, l_1_bit_full_adder_1807bcc1_32_cout, xor_3_out, xor_4_out,
       xor_5_out, xor_6_out, xor_7_out, xor_8_out, xor_9_out, xor_10_out, xor_11_out, xor_12_out, xor_13_out,
       xor_14_out, xor_15_out, xor_16_out, xor_17_out, xor_18_out, xor_19_out, xor_20_out, xor_21_out,
       xor_22_out, xor_23_out, xor_24_out, xor_25_out, xor_26_out, xor_27_out, xor_28_out, xor_29_out,
       xor_30_out, xor_31_out, xor_32_out, xor_33_out, xor_34_out, xor_35_out;

  xor xor_1 (OF, l_1_bit_full_adder_1807bcc1_2_cout, l_1_bit_full_adder_1807bcc1_1_cout);
  xor xor_2 (Cout, Sub, l_1_bit_full_adder_1807bcc1_1_cout);
  xor xor_3 (xor_3_out, B[31], Sub);
  L_1_Bit_Full_Adder_1807bcc1 l_1_bit_full_adder_1807bcc1_1 (
    .A(xor_3_out), .B(A[31]), .S(S[31]), .Cout(l_1_bit_full_adder_1807bcc1_1_cout),
    .Cin(l_1_bit_full_adder_1807bcc1_2_cout));
  xor xor_4 (xor_4_out, B[30], Sub);
  L_1_Bit_Full_Adder_1807bcc1 l_1_bit_full_adder_1807bcc1_2 (
    .A(xor_4_out), .B(A[30]), .S(S[30]), .Cout(l_1_bit_full_adder_1807bcc1_2_cout),
    .Cin(l_1_bit_full_adder_1807bcc1_3_cout));
  xor xor_5 (xor_5_out, B[29], Sub);
  L_1_Bit_Full_Adder_1807bcc1 l_1_bit_full_adder_1807bcc1_3 (
    .A(xor_5_out), .B(A[29]), .S(S[29]), .Cout(l_1_bit_full_adder_1807bcc1_3_cout),
    .Cin(l_1_bit_full_adder_1807bcc1_4_cout));
  xor xor_6 (xor_6_out, B[28], Sub);
  L_1_Bit_Full_Adder_1807bcc1 l_1_bit_full_adder_1807bcc1_4 (
    .A(xor_6_out), .B(A[28]), .S(S[28]), .Cout(l_1_bit_full_adder_1807bcc1_4_cout),
    .Cin(l_1_bit_full_adder_1807bcc1_5_cout));
  xor xor_7 (xor_7_out, B[27], Sub);
  L_1_Bit_Full_Adder_1807bcc1 l_1_bit_full_adder_1807bcc1_5 (
    .A(xor_7_out), .B(A[27]), .S(S[27]), .Cout(l_1_bit_full_adder_1807bcc1_5_cout),
    .Cin(l_1_bit_full_adder_1807bcc1_6_cout));
  xor xor_8 (xor_8_out, B[26], Sub);
  L_1_Bit_Full_Adder_1807bcc1 l_1_bit_full_adder_1807bcc1_6 (
    .A(xor_8_out), .B(A[26]), .S(S[26]), .Cout(l_1_bit_full_adder_1807bcc1_6_cout),
    .Cin(l_1_bit_full_adder_1807bcc1_7_cout));
  xor xor_9 (xor_9_out, B[25], Sub);
  L_1_Bit_Full_Adder_1807bcc1 l_1_bit_full_adder_1807bcc1_7 (
    .A(xor_9_out), .B(A[25]), .S(S[25]), .Cout(l_1_bit_full_adder_1807bcc1_7_cout),
    .Cin(l_1_bit_full_adder_1807bcc1_8_cout));
  xor xor_10 (xor_10_out, B[24], Sub);
  L_1_Bit_Full_Adder_1807bcc1 l_1_bit_full_adder_1807bcc1_8 (
    .A(xor_10_out), .B(A[24]), .S(S[24]), .Cout(l_1_bit_full_adder_1807bcc1_8_cout),
    .Cin(l_1_bit_full_adder_1807bcc1_9_cout));
  xor xor_11 (xor_11_out, B[23], Sub);
  L_1_Bit_Full_Adder_1807bcc1 l_1_bit_full_adder_1807bcc1_9 (
    .A(xor_11_out), .B(A[23]), .S(S[23]), .Cout(l_1_bit_full_adder_1807bcc1_9_cout),
    .Cin(l_1_bit_full_adder_1807bcc1_10_cout));
  xor xor_12 (xor_12_out, B[22], Sub);
  L_1_Bit_Full_Adder_1807bcc1 l_1_bit_full_adder_1807bcc1_10 (
    .A(xor_12_out), .B(A[22]), .S(S[22]), .Cout(l_1_bit_full_adder_1807bcc1_10_cout),
    .Cin(l_1_bit_full_adder_1807bcc1_11_cout));
  xor xor_13 (xor_13_out, B[21], Sub);
  L_1_Bit_Full_Adder_1807bcc1 l_1_bit_full_adder_1807bcc1_11 (
    .A(xor_13_out), .B(A[21]), .S(S[21]), .Cout(l_1_bit_full_adder_1807bcc1_11_cout),
    .Cin(l_1_bit_full_adder_1807bcc1_12_cout));
  xor xor_14 (xor_14_out, B[20], Sub);
  L_1_Bit_Full_Adder_1807bcc1 l_1_bit_full_adder_1807bcc1_12 (
    .A(xor_14_out), .B(A[20]), .S(S[20]), .Cout(l_1_bit_full_adder_1807bcc1_12_cout),
    .Cin(l_1_bit_full_adder_1807bcc1_13_cout));
  xor xor_15 (xor_15_out, B[19], Sub);
  L_1_Bit_Full_Adder_1807bcc1 l_1_bit_full_adder_1807bcc1_13 (
    .A(xor_15_out), .B(A[19]), .S(S[19]), .Cout(l_1_bit_full_adder_1807bcc1_13_cout),
    .Cin(l_1_bit_full_adder_1807bcc1_14_cout));
  xor xor_16 (xor_16_out, B[18], Sub);
  L_1_Bit_Full_Adder_1807bcc1 l_1_bit_full_adder_1807bcc1_14 (
    .A(xor_16_out), .B(A[18]), .S(S[18]), .Cout(l_1_bit_full_adder_1807bcc1_14_cout),
    .Cin(l_1_bit_full_adder_1807bcc1_15_cout));
  xor xor_17 (xor_17_out, B[17], Sub);
  L_1_Bit_Full_Adder_1807bcc1 l_1_bit_full_adder_1807bcc1_15 (
    .A(xor_17_out), .B(A[17]), .S(S[17]), .Cout(l_1_bit_full_adder_1807bcc1_15_cout),
    .Cin(l_1_bit_full_adder_1807bcc1_16_cout));
  xor xor_18 (xor_18_out, B[16], Sub);
  L_1_Bit_Full_Adder_1807bcc1 l_1_bit_full_adder_1807bcc1_16 (
    .A(xor_18_out), .B(A[16]), .S(S[16]), .Cout(l_1_bit_full_adder_1807bcc1_16_cout),
    .Cin(l_1_bit_full_adder_1807bcc1_17_cout));
  xor xor_19 (xor_19_out, B[15], Sub);
  L_1_Bit_Full_Adder_1807bcc1 l_1_bit_full_adder_1807bcc1_17 (
    .A(xor_19_out), .B(A[15]), .S(S[15]), .Cout(l_1_bit_full_adder_1807bcc1_17_cout),
    .Cin(l_1_bit_full_adder_1807bcc1_18_cout));
  xor xor_20 (xor_20_out, B[14], Sub);
  L_1_Bit_Full_Adder_1807bcc1 l_1_bit_full_adder_1807bcc1_18 (
    .A(xor_20_out), .B(A[14]), .S(S[14]), .Cout(l_1_bit_full_adder_1807bcc1_18_cout),
    .Cin(l_1_bit_full_adder_1807bcc1_19_cout));
  xor xor_21 (xor_21_out, B[13], Sub);
  L_1_Bit_Full_Adder_1807bcc1 l_1_bit_full_adder_1807bcc1_19 (
    .A(xor_21_out), .B(A[13]), .S(S[13]), .Cout(l_1_bit_full_adder_1807bcc1_19_cout),
    .Cin(l_1_bit_full_adder_1807bcc1_20_cout));
  xor xor_22 (xor_22_out, B[12], Sub);
  L_1_Bit_Full_Adder_1807bcc1 l_1_bit_full_adder_1807bcc1_20 (
    .A(xor_22_out), .B(A[12]), .S(S[12]), .Cout(l_1_bit_full_adder_1807bcc1_20_cout),
    .Cin(l_1_bit_full_adder_1807bcc1_21_cout));
  xor xor_23 (xor_23_out, B[11], Sub);
  L_1_Bit_Full_Adder_1807bcc1 l_1_bit_full_adder_1807bcc1_21 (
    .A(xor_23_out), .B(A[11]), .S(S[11]), .Cout(l_1_bit_full_adder_1807bcc1_21_cout),
    .Cin(l_1_bit_full_adder_1807bcc1_22_cout));
  xor xor_24 (xor_24_out, B[10], Sub);
  L_1_Bit_Full_Adder_1807bcc1 l_1_bit_full_adder_1807bcc1_22 (
    .A(xor_24_out), .B(A[10]), .S(S[10]), .Cout(l_1_bit_full_adder_1807bcc1_22_cout),
    .Cin(l_1_bit_full_adder_1807bcc1_23_cout));
  xor xor_25 (xor_25_out, B[9], Sub);
  L_1_Bit_Full_Adder_1807bcc1 l_1_bit_full_adder_1807bcc1_23 (
    .A(xor_25_out), .B(A[9]), .S(S[9]), .Cout(l_1_bit_full_adder_1807bcc1_23_cout),
    .Cin(l_1_bit_full_adder_1807bcc1_24_cout));
  xor xor_26 (xor_26_out, B[8], Sub);
  L_1_Bit_Full_Adder_1807bcc1 l_1_bit_full_adder_1807bcc1_24 (
    .A(xor_26_out), .B(A[8]), .S(S[8]), .Cout(l_1_bit_full_adder_1807bcc1_24_cout),
    .Cin(l_1_bit_full_adder_1807bcc1_25_cout));
  xor xor_27 (xor_27_out, B[7], Sub);
  L_1_Bit_Full_Adder_1807bcc1 l_1_bit_full_adder_1807bcc1_25 (
    .A(xor_27_out), .B(A[7]), .S(S[7]), .Cout(l_1_bit_full_adder_1807bcc1_25_cout),
    .Cin(l_1_bit_full_adder_1807bcc1_26_cout));
  xor xor_28 (xor_28_out, B[6], Sub);
  L_1_Bit_Full_Adder_1807bcc1 l_1_bit_full_adder_1807bcc1_26 (
    .A(xor_28_out), .B(A[6]), .S(S[6]), .Cout(l_1_bit_full_adder_1807bcc1_26_cout),
    .Cin(l_1_bit_full_adder_1807bcc1_27_cout));
  xor xor_29 (xor_29_out, B[5], Sub);
  L_1_Bit_Full_Adder_1807bcc1 l_1_bit_full_adder_1807bcc1_27 (
    .A(xor_29_out), .B(A[5]), .S(S[5]), .Cout(l_1_bit_full_adder_1807bcc1_27_cout),
    .Cin(l_1_bit_full_adder_1807bcc1_28_cout));
  xor xor_30 (xor_30_out, B[4], Sub);
  L_1_Bit_Full_Adder_1807bcc1 l_1_bit_full_adder_1807bcc1_28 (
    .A(xor_30_out), .B(A[4]), .S(S[4]), .Cout(l_1_bit_full_adder_1807bcc1_28_cout),
    .Cin(l_1_bit_full_adder_1807bcc1_29_cout));
  xor xor_31 (xor_31_out, B[3], Sub);
  L_1_Bit_Full_Adder_1807bcc1 l_1_bit_full_adder_1807bcc1_29 (
    .A(xor_31_out), .B(A[3]), .S(S[3]), .Cout(l_1_bit_full_adder_1807bcc1_29_cout),
    .Cin(l_1_bit_full_adder_1807bcc1_30_cout));
  xor xor_32 (xor_32_out, B[2], Sub);
  L_1_Bit_Full_Adder_1807bcc1 l_1_bit_full_adder_1807bcc1_30 (
    .A(xor_32_out), .B(A[2]), .S(S[2]), .Cout(l_1_bit_full_adder_1807bcc1_30_cout),
    .Cin(l_1_bit_full_adder_1807bcc1_31_cout));
  xor xor_33 (xor_33_out, B[1], Sub);
  L_1_Bit_Full_Adder_1807bcc1 l_1_bit_full_adder_1807bcc1_31 (
    .A(xor_33_out), .B(A[1]), .S(S[1]), .Cout(l_1_bit_full_adder_1807bcc1_31_cout),
    .Cin(l_1_bit_full_adder_1807bcc1_32_cout));
  xor xor_34 (xor_34_out, B[0], Sub);
  L_1_Bit_Full_Adder_1807bcc1 l_1_bit_full_adder_1807bcc1_32 (
    .A(xor_34_out), .B(A[0]), .S(S[0]), .Cout(l_1_bit_full_adder_1807bcc1_32_cout), .Cin(xor_35_out));
  xor xor_35 (xor_35_out, 1'b0, Sub);
endmodule
