// Logisim project Assignment 1-1.circ as structural Verilog: 1 circuit, main circuit main
module main (
  input  [31:0] in_1,
  input  [31:0] in_2,
  input  [31:0] in_3,
  input  [31:0] in_4,
  input  [2:0] in_5,
  output [31:0] out_6
);

  wire clock_1_out;
  wire [31:0] adder_1_out, and_1_out, divider_1_out, multiplier_1_out, negator_1_out, not_1_out, or_1_out,
       subtractor_1_out;

  Subtractor #(.width(32)) subtractor_1 (.a(in_1), .b(in_2), .out(subtractor_1_out));  // open: bin, bout
  Adder #(.width(32)) adder_1 (.a(in_1), .b(in_2), .out(adder_1_out));  // open: cin, cout
  Multiplier #(.width(32)) multiplier_1 (.a(in_1), .b(in_2), .out(multiplier_1_out), .cout(in_4));  // open: cin
  Divider #(.width(32)) divider_1 (.a(in_1), .b(in_2), .out(divider_1_out), .rem(in_3));  // open: upper
  assign not_1_out = ~in_1;  // NOT_Gate not_1, 32 bits wide
  assign or_1_out = in_1 | in_2;  // OR_Gate or_1, 32 bits wide
  assign and_1_out = in_1 & in_2;  // AND_Gate and_1, 32 bits wide
  Negator #(.width(32)) negator_1 (.in(in_1), .out(negator_1_out));
  Clock clock_1 (.out(clock_1_out));
  Multiplexer #(.select(3), .width(32)) multiplexer_1 (
    .in0(not_1_out), .in1(or_1_out), .in2(and_1_out), .in3(subtractor_1_out), .in4(negator_1_out),
    .in5(adder_1_out), .in6(multiplier_1_out), .in7(divider_1_out), .out(out_6), .sel(in_5), .en(clock_1_out));
endmodule
