// Logisim project part-1.circ as structural Verilog: 1 circuit, main circuit main
module main (
  input  in_1,
  input  in_2,
  input  in_3,
  input  in_4,
  input  [2:0] in_5,
  output out_6
);

  wire adder_1_out, and_1_out, clock_1_out, divider_1_out, multiplier_1_out, negator_1_out, not_1_out,
       or_1_out, subtractor_1_out;

  Subtractor #(.width(1)) subtractor_1 (.a(in_1), .b(in_2), .out(subtractor_1_out));  // open: bin, bout
  Adder #(.width(1)) adder_1 (.a(in_1), .b(in_2), .out(adder_1_out));  // open: cin, cout
  Multiplier #(.width(1)) multiplier_1 (.a(in_1), .b(in_2), .out(multiplier_1_out), .cout(in_4));  // open: cin
  Divider #(.width(1)) divider_1 (.a(in_1), .b(in_2), .out(divider_1_out), .rem(in_3));  // open: upper
  not not_1 (not_1_out, in_1);
  or or_1 (or_1_out, in_1, in_2);
  and and_1 (and_1_out, in_1, in_2);
  Negator #(.width(1)) negator_1 (.in(in_1), .out(negator_1_out));
  Clock clock_1 (.out(clock_1_out));
  Multiplexer #(.select(3)) multiplexer_1 (
    .in0(not_1_out), .in1(or_1_out), .in2(and_1_out), .in3(subtractor_1_out), .in4(negator_1_out),
    .in5(adder_1_out), .in6(multiplier_1_out), .in7(divider_1_out), .out(out_6), .sel(in_5), .en(clock_1_out));
endmodule
